# Fritzing sketch LightGateSend (saved by Fritzing 0.7.5b)
breadboards: 1

parts:
  Nano1 = Arduino Nano v2.3
  R1 = Resistor [tolerance=±5% resistance=1k package=THT]
  LED1 = LED - 5mm [color="Infrared (940nm)" package="5 mm [THT]"]
  Q1 = NPN-Transistor [package="TO92 [THT]"]
  VCC1 = Battery block 9V

nets:
  N1: Nano1.GND, Q1.C, VCC1.-
  N2: Nano1.D3, R1.Pin_0
  N3: Nano1.+5V, LED1.anode
  N4: Nano1.VIN, VCC1.+
  N5: R1.Pin_1, Q1.B
  N6: LED1.cathode, Q1.E

// code stored in the sketch: LightGateSend.ino
/*
  LightGate Send

  This sketch will create a 38kHz carrier from an IR LED
  Code adapted from tutorial at http://www.ladyada.net/learn/sensors/ir.html
  
  

  The circuit:
  * no input
  * TSAL6200 IR LED   powered by 5V out
  * IR LED controlled by BC548B NPN transistor on pin 3
  * 1k resistor between pin3 and transistor base

  Created 17 Apr 2017
  By Courses4Horses geoff.goldrick@gmail.com
  Modified day month year
  By author's name

*/

const int IRledPin =  3;    // LED connected to digital pin 3

// 38 kHz is about 13 microseconds high and 13 microseconds low
// digitalWrite takes about 3 secs therefore delay time should be 10 secs
const long interval = 10; //interval in micorsecs at which to change LEd state
unsigned long previousMicros = 0;
int ledState = LOW;   //used to change the LED





void setup() {
  pinMode(IRledPin, OUTPUT);      
  Serial.begin(9600);
}

void loop() {

  //check to see if it is time to change the LED
  unsigned long currentMicros = micros();

  if (currentMicros - previousMicros >= interval) {
    // save the last time you blinked the LED
    previousMicros = currentMicros;
    ledState = !ledState;

    // set the LED with the ledState of the variable:
    digitalWrite(IRledPin, ledState);
  }

  
     
     // so 26 microseconds altogether
     //TODO use serial print to check the delay
     //TODO rewrite without delay to properly time cycle
}
